# Fritzing sketch togglButton (saved by Fritzing 0.9.4)
breadboards: 1

parts:
  U3 = NodeMCU V1.0
  S1 = Round Pushbutton
  LED1 = smd LED [color="Red (633nm)" package="0603 [SMD]"]  # not connected
  R1 = Resistor [tolerance=±5% resistance=10k package="0402 [SMD]"]

nets:
  N1: U3.3V3, S1.leg1
  N2: U3.GND, R1.Pin_0
  N3: S1.leg0, R1.Pin_1

custom parts:
  NodeMCU V1.0: ESP8266 based NodeMCU
